# Fritzing sketch LED-Relay_Webserver (saved by Fritzing 0.9.3b)
breadboards: 1

parts:
  M1 = MAX7219 8x8 single Led Matrix Module
  M2 = MAX7219 8x8 single Led Matrix Module  # not connected
  M3 = MAX7219 8x8 single Led Matrix Module  # not connected
  M4 = MAX7219 8x8 single Led Matrix Module  # not connected
  Mod1 = Amica NodeMCU DevKit 1.0  # not connected
  U1 = 4-Channel 5v Relay Shield [package=relay-4ch5v10a]
  Part1 = Adafruit Micro USB Breakout [part_number="Adafruit #1833"]

nets:
  GND: M1.I-GND, M1.O-GND, U1.GND, Part1.GND
  N1: M1.I-VCC, M1.O-VCC, U1.VCC, Part1.VBUS

custom parts:
  MAX7219 8x8 single Led Matrix Module: Description: MAX7219 8x8 LedMatrix single Red Module Dimensions: 32x32mm Documents:
  Amica NodeMCU DevKit 1.0: Amica NodeMCU DevKit 1.0 Development Kit based on ESP8266 ESP-12E, integating GPIO, PWM, IIC, 1-Wire and ADC all in one board. Links: NodeMCU information page Github
  4-Channel 5v Relay Shield: 4 Channel 5v Relay Shield w. 2x SPD-06VDC-SD-C
  Adafruit Micro USB Breakout: Simple but effective - this breakout board has a USB Micro-B connector, with all 5 pins broken out. Great for pairing with a microcontroller with USB support, or adding USB 5V power to a project. We use a micro-AB connector with through-hole shielding pads for an excellent strong connection - it won't rip off by accident! Comes with one fully assembled and tested micro B breakout PCB and a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
